// Logisim project RAM - ukeoppgaver 5.circ as structural Verilog: 2 circuits, main circuit main
module main (
);

  _3a___RAM u_3a_ram_1 ();  // open: Adresse, Chip_select__0_disable_comp, RESET__on_1, Load_0___Write_1, Output, Input
  RAM #(.addrWidth(4), .dataWidth(4), .bus("asynch")) ram_1 ();  // open: addr, data, sel, ld, clr
endmodule

module _3a___RAM (
  input  [3:0] Adresse,
  input  Chip_select__0_disable_comp,
  input  [3:0] Input,
  input  RESET__on_1,
  input  Load_0___Write_1,
  output [3:0] Output
);

  wire not_1_out;

  RAM #(.addrWidth(4), .dataWidth(4), .bus("asynch")) ram_1 (
    .addr(Adresse), .data(Output), .sel(Chip_select__0_disable_comp), .ld(not_1_out), .clr(RESET__on_1));
  not not_1 (not_1_out, Load_0___Write_1);
  assign Output = Load_0___Write_1 ? Input : 4'bz;  // Controlled_Buffer controlled_buffer_1
endmodule
