// Logisim project Ukesoppgaver3.circ as structural Verilog
module D_Latch (
  input  D,
  input  CLK,
  output Q
);

  wire nand_1_out, nand_2_out, nand_4_out, not_1_out;

  not not_1 (not_1_out, D);
  nand nand_1 (nand_1_out, D, CLK);
  nand nand_2 (nand_2_out, not_1_out, CLK);
  nand nand_3 (Q, nand_1_out, nand_4_out);
  nand nand_4 (nand_4_out, Q, nand_2_out);
endmodule

module D_Flip_Flop (
  input  D,
  input  ACLEAR,
  output out_3
);

  wire and_1_out, Clock_out, d_latch_1_q, d_latch_2_q, not_1_out, not_2_out;

  Clock Clock (.out(Clock_out));
  D_Latch d_latch_1 (.D(D), .CLK(Clock_out), .Q(d_latch_1_q));
  not not_1 (not_1_out, Clock_out);
  D_Latch d_latch_2 (.D(d_latch_1_q), .CLK(not_1_out), .Q(d_latch_2_q));
  and and_1 (and_1_out, d_latch_2_q, ACLEAR);
  and and_2 (out_3, d_latch_2_q, not_2_out);
  not not_2 (not_2_out, and_1_out);
endmodule

module D_Flipflop_Synkron (
  input  CLEAR,
  input  D,
  output Q
);

  wire and_1_out, clock_1_out, d_latch_1_q, not_1_out, not_2_out;

  not not_1 (not_1_out, CLEAR);
  Clock clock_1 (.out(clock_1_out));
  and and_1 (and_1_out, not_1_out, D);
  D_Latch d_latch_1 (.D(and_1_out), .CLK(clock_1_out), .Q(d_latch_1_q));
  not not_2 (not_2_out, clock_1_out);
  D_Latch d_latch_2 (.D(d_latch_1_q), .CLK(not_2_out), .Q(Q));
endmodule

module D_flipflop_4 (
  input  SET,
  input  D,
  output Q
);

  wire clock_1_out, d_latch_1_q, not_1_out, or_1_out;

  or or_1 (or_1_out, SET, D);
  Clock clock_1 (.out(clock_1_out));
  D_Latch d_latch_1 (.D(or_1_out), .CLK(clock_1_out), .Q(d_latch_1_q));
  not not_1 (not_1_out, clock_1_out);
  D_Latch d_latch_2 (.D(d_latch_1_q), .CLK(not_1_out), .Q(Q));
endmodule

module D_flipflop_5 (
  input  CE,
  input  D,
  output Q
);

  wire and_1_out, and_2_out, clock_1_out, d_latch_1_q, not_1_out, not_2_out, or_1_out;

  Clock clock_1 (.out(clock_1_out));
  not not_1 (not_1_out, CE);
  and and_1 (and_1_out, not_1_out, Q);
  and and_2 (and_2_out, CE, D);
  or or_1 (or_1_out, and_1_out, and_2_out);
  D_Latch d_latch_1 (.D(or_1_out), .CLK(clock_1_out), .Q(d_latch_1_q));
  not not_2 (not_2_out, clock_1_out);
  D_Latch d_latch_2 (.D(d_latch_1_q), .CLK(not_2_out), .Q(Q));
endmodule
