// Logisim project uke9arkitektur.circ as structural Verilog: 14 circuits, main circuit main
module main (
  input  a0,
  input  a1,
  input  a2,
  input  a3,
  input  [3:0] in_5,
  input  RESET
);

  wire clock_1_out;
  wire [3:0] if15_1_out_3;

  Clock clock_1 (.out(clock_1_out));
  counter counter_1 (.CLK(clock_1_out), .\input (if15_1_out_3), .out_4(in_5), .Reset(RESET));
  If15 if15_1 (.INPUT({a3, a2, a1, a0}), .out_3(if15_1_out_3), .OUTPUT(in_5));
endmodule

module Oppgave1b (
  input  RESET,
  output [3:0] out_2
);

  wire and_1_out, clock_1_out, nand_1_out;

  Clock clock_1 (.out(clock_1_out));
  nand nand_1 (nand_1_out, out_2[0], out_2[1], out_2[2], out_2[3]);
  and and_1 (and_1_out, nand_1_out, clock_1_out);
  Counter #(.width(4), .max('hf)) counter_1 (.Q(out_2), .clk(and_1_out), .clr(RESET));  // open: load, D, count, carry
endmodule

// 4-bit Counter
module counter (
  input  Reset,
  input  CLK,
  input  [3:0] \input ,
  output [3:0] out_4
);

  wire [3:0] register_1_q;

  Register #(.width(4)) register_1 (.D(out_4), .Q(register_1_q), .clk(CLK), .clr(Reset));  // open: en
  _4_bits_adder u_4_bits_adder_1 (
    .a0(register_1_q[0]), .b0(\input [0]), .a1(register_1_q[1]), .b1(\input [1]), .a2(register_1_q[2]),
    .b2(\input [2]), .a3(register_1_q[3]), .b3(\input [3]), .s1(out_4[0]), .s2(out_4[1]), .s3(out_4[2]),
    .s4(out_4[3]));  // open: Carry
endmodule

module If15 (
  input  [3:0] OUTPUT,
  input  [3:0] INPUT,
  output [3:0] out_3
);

  wire and_1_out;

  tristate tristate_1 (.Input(INPUT[0]), .Lock_Signal(and_1_out), .Ouput(out_3[0]));
  tristate tristate_2 (.Input(INPUT[1]), .Lock_Signal(and_1_out), .Ouput(out_3[1]));
  and and_1 (and_1_out, OUTPUT[0], OUTPUT[1], OUTPUT[2], OUTPUT[3]);
  tristate tristate_3 (.Input(INPUT[2]), .Lock_Signal(and_1_out), .Ouput(out_3[2]));
  tristate tristate_4 (.Input(INPUT[3]), .Lock_Signal(and_1_out), .Ouput(out_3[3]));
endmodule

module tristate (
  input  Input,
  input  Lock_Signal,
  output Ouput
);

  wire not_1_out;

  not not_1 (not_1_out, Lock_Signal);
  assign Ouput = not_1_out ? Input : 1'bz;  // Controlled_Buffer controlled_buffer_1
  assign Ouput = Lock_Signal ? 1'b0 : 1'bz;  // Controlled_Buffer controlled_buffer_2
endmodule

// 4-bit adder
module _4_bits_adder (
  input  a0,
  input  b0,
  input  a1,
  input  b1,
  input  a2,
  input  b2,
  input  a3,
  input  b3,
  output s1,
  output s2,
  output s3,
  output s4,
  output Carry
);

  wire fulladder_1_c_1, fulladder_2_c_1, halfadder_1_c;

  Halfadder halfadder_1 (.A(a0), .B(b0), .S(s1), .C(halfadder_1_c));
  Fulladder fulladder_1 (.C(halfadder_1_c), .A(a1), .B(b1), .S_n(s2), .C_1(fulladder_1_c_1));
  Fulladder fulladder_2 (.C(fulladder_1_c_1), .A(a2), .B(b2), .S_n(s3), .C_1(fulladder_2_c_1));
  Fulladder fulladder_3 (.C(fulladder_2_c_1), .A(a3), .B(b3), .S_n(s4), .C_1(Carry));
endmodule

// 4b register
module _4_bit_register (
  input  [3:0] D_in,
  input  Clock,
  input  RESET,
  output [3:0] out_4
);

  D_Flipflop d_flipflop_1 (.D(Clock), .Clk(Clock), .ACLEAR(RESET), .out_4(out_4[0]));
  D_Flipflop d_flipflop_2 (.D(D_in[1]), .Clk(Clock), .ACLEAR(RESET), .out_4(out_4[1]));
  D_Flipflop d_flipflop_3 (.D(D_in[2]), .Clk(Clock), .ACLEAR(RESET), .out_4(out_4[2]));
  D_Flipflop d_flipflop_4 (.D(D_in[3]), .Clk(Clock), .ACLEAR(RESET), .out_4(out_4[3]));

  assign D_in[0] = Clock;
endmodule

module D_latch (
  input  D,
  input  CLK,
  output Q
);

  wire nand_1_out, nand_2_out, nand_4_out, not_1_out;

  not not_1 (not_1_out, D);
  nand nand_1 (nand_1_out, D, CLK);
  nand nand_2 (nand_2_out, not_1_out, CLK);
  nand nand_3 (Q, nand_1_out, nand_4_out);
  nand nand_4 (nand_4_out, Q, nand_2_out);
endmodule

module D_Flipflop (
  input  D,
  input  Clk,
  input  ACLEAR,
  output out_4
);

  wire and_1_out, d_latch_1_q, d_latch_2_q, not_1_out, not_2_out;

  D_latch d_latch_1 (.D(D), .CLK(Clk), .Q(d_latch_1_q));
  not not_1 (not_1_out, Clk);
  D_latch d_latch_2 (.D(d_latch_1_q), .CLK(not_1_out), .Q(d_latch_2_q));
  and and_1 (and_1_out, d_latch_2_q, ACLEAR);
  and and_2 (out_4, d_latch_2_q, not_2_out);
  not not_2 (not_2_out, and_1_out);
endmodule

// FA
module Fulladder (
  input  C,
  input  A,
  input  B,
  output S_n,
  output C_1
);

  wire and_1_out, halfadder_1_c, halfadder_1_s;

  Halfadder halfadder_1 (.A(A), .B(B), .S(halfadder_1_s), .C(halfadder_1_c));
  xor xor_1 (S_n, halfadder_1_s, C);
  and and_1 (and_1_out, halfadder_1_s, C);
  or or_1 (C_1, and_1_out, halfadder_1_c);
endmodule

// HA
module Halfadder (
  input  A,
  input  B,
  output S,
  output C
);

  xor xor_1 (S, A, B);
  and and_1 (C, A, B);
endmodule

module Oppgave1 (
  input  a0,
  input  a1,
  input  a2,
  input  a3,
  input  RESET,
  output [3:0] out_6
);

  wire clock_1_out;

  Clock clock_1 (.out(clock_1_out));
  counter counter_1 (.CLK(clock_1_out), .\input ({a3, a2, a1, a0}), .out_4(out_6), .Reset(RESET));
  // Probe on out_6
endmodule

module _2a___Tristate (
  input  Enable_1,
  input  [3:0] Input_1,
  input  [3:0] Input_2,
  input  Enable_2,
  output [3:0] Output_1,
  output [3:0] Output_2
);

  assign Output_1[0] = Enable_1 ? Input_1[0] : 1'bz;  // Controlled_Buffer controlled_buffer_1
  assign Output_1[1] = Enable_1 ? Input_1[1] : 1'bz;  // Controlled_Buffer controlled_buffer_2
  assign Output_1[2] = Enable_1 ? Input_1[2] : 1'bz;  // Controlled_Buffer controlled_buffer_3
  assign Output_1[3] = Enable_1 ? Input_1[3] : 1'bz;  // Controlled_Buffer controlled_buffer_4
  assign Output_2[0] = Enable_2 ? Input_2[0] : 1'bz;  // Controlled_Buffer controlled_buffer_5
  assign Output_2[1] = Enable_2 ? Input_2[1] : 1'bz;  // Controlled_Buffer controlled_buffer_6
  assign Output_2[2] = Enable_2 ? Input_2[2] : 1'bz;  // Controlled_Buffer controlled_buffer_7
  assign Output_2[3] = Enable_2 ? Input_2[3] : 1'bz;  // Controlled_Buffer controlled_buffer_8
endmodule

module _2b___2_1_MUX (
  input  SELECT
);

  _2a___Tristate u_2a_tristate_1 ();  // open: Input_1, Input_2, Enable_1, Enable_2, Output_1, Output_2
  _2a___Tristate u_2a_tristate_2 (.Enable_2(SELECT));  // open: Input_1, Input_2, Enable_1, Output_1, Output_2
endmodule
